// Logisim project CPU_Pipeline_12192143.circ as structural Verilog: 29 circuits, main circuit Computer
module Computer (
  input  Reset
);

  wire ALUSrc_EX, ALUSrc_IF, and_2_out, and_4_out, Branch_EX, Branch_ID, Branch_IF, Choice_ID, Choice_IF,
       CLK, clock_1_out, clock_2_out, comparator_1_eq, comparator_2_eq, comparator_3_eq, comparator_4_eq,
       comparator_5_eq, comparator_6_eq, comparator_7_eq, CondFit_EX, CondFit_IF, cpu_alu_1_zeroflag,
       ex_mem_1_memread_out, ex_mem_1_memreg_out, ex_mem_1_memwrite_out, ex_mem_1_opbyte_out,
       ex_mem_1_opmemory_out, ex_mem_1_regwrite_out, ex_mem_1_stp_out, id_ex_1_choice_out, id_ex_1_jcond_out,
       id_ex_1_memread_out, id_ex_1_memreg_out, id_ex_1_memwrite_out, id_ex_1_opbyte_out,
       id_ex_1_opmemory_out, id_ex_1_regdst_out, id_ex_1_regwrite_out, id_ex_1_stp_out, if_id_1_alusrc_out,
       if_id_1_immpos_out, if_id_1_isxor_out, if_id_1_jcond_out, if_id_1_memreg_out, if_id_1_opbyte_out,
       if_id_1_opmemory_out, if_id_1_regdst_out, ImmPos_EX, ImmPos_IF, isXor_EX, isXor_IF, Jcond_IF,
       mem_wb_1_regwrite_out, MemRead_ID, MemRead_IF, MemReg_IF, MemWrite_ID, MemWrite_IF, multiplexer_4_out,
       multiplexer_17_out, not_1_out, not_2_out, not_3_out, not_4_out, not_5_out, not_6_out, not_7_out,
       not_8_out, not_9_out, or_1_out, or_2_out, Pretested_Branch_ID, Pretested_Choice_ID,
       Pretested_MemRead_ID, Pretested_MemWrite_ID, Pretested_RegWrite_ID, Pretested_STP_ID, RegDst_IF,
       RegWrite_ID, RegWrite_IF, riskcontrolunit_1_is_risk, STP, STP_ID, STP_IF, xor_2_out;
  wire [1:0] ForwardA_EX, ForwardB_EX;
  wire [2:0] ALUOp_IF;
  wire [3:0] id_ex_1_innerop_out, if_id_1_innerop_out, InnerOp_IF;
  wire [4:0] ex_mem_1_regwaddr_out, id_ex_1_rd_out, id_ex_1_rs_out, id_ex_1_rt_out, if_id_1_rd_out,
       if_id_1_rs_out, if_id_1_rt_out, mem_wb_1_regwaddr_out, multiplexer_13_out, rs_IF, rt_IF;
  wire [5:0] fruc_IF, opcode_IF;
  wire [15:0] if_id_1_rawimm_out, rawImm_EX;
  wire [15:6] rawImm_IF;
  wire [31:0] bit_extender_1_out, bit_extender_2_out, Choiced_PC_IF, Count, cpu_alu_1_result,
       cpu_rigisterfile_1_rdata1, cpu_rigisterfile_1_rdata2, ex_mem_1_memwritedata_out, ex_mem_1_res_out,
       id_ex_1_rdata1_out, id_ex_1_rdata2_out, if_id_1_npc_out, Imm_EX, Imm_IF, jmpPC_EX, jmpPC_IF,
       mem_wb_1_writebackdate_out, multiplexer_16_out, multiplexer_19_out, multiplexer_20_out, nPC_EX,
       nPC_IF, OpNum1_EX, OpNum2_EX, PC_EX, PC_IF, PC_q, Pxor_OpNum2_EX, shifter_1_out, shifter_2_out,
       shifter_3_out, shifter_4_out, used_ram_1_dataout, xor_1_out;

  Clock clock_1 (.out(clock_1_out));
  Clock clock_2 (.out(clock_2_out));
  Counter #(.max('hffffffff), .width(32)) counter_1 (
    .clr(Reset), .load(1'b0), .up(1'b1), .count(not_1_out), .clk(CLK), .Q(Count));  // open: D, carry
  not not_1 (not_1_out, STP);
  Register #(.width(32)) PC (.D(Choiced_PC_IF), .en(not_2_out), .clk(CLK), .Q(PC_q));  // open: clr
  not not_2 (not_2_out, and_2_out);
  not not_3 (not_3_out, STP);
  and and_1 (CLK, not_3_out, clock_2_out);
  Multiplexer #(.width(32)) multiplexer_1 (.in0(PC_q), .in1(multiplexer_19_out), .out(PC_IF), .sel(xor_2_out));
  BTB btb_1 (
    .PC_IF(PC_IF), .Branch_IF(Branch_IF), .PC_EX(PC_EX), .Branch_EX(Branch_EX), .Cond(CondFit_EX),
    .CLK(clock_1_out), .CondFit(CondFit_IF));
  // Probe on Count
  ROM #(.addrWidth(14), .dataWidth(32)) rom_1 (
    .addr(PC_IF[15:2]), .data({opcode_IF, rs_IF, rt_IF, rawImm_IF, fruc_IF}));
  Adder #(.width(32)) adder_1 (.a(32'h4), .b(PC_IF), .out(nPC_IF));  // open: cin, cout
  assign bit_extender_1_out = {{16{rawImm_IF[15]}}, {rawImm_IF, fruc_IF}};  // Bit_Extender bit_extender_1
  Shifter #(.width(32)) shifter_1 (.in(Imm_IF), .\dist (5'b00010), .out(shifter_1_out));
  Multiplexer #(.width(32)) multiplexer_2 (
    .in0(bit_extender_1_out), .in1(shifter_2_out), .out(Imm_IF), .sel(ImmPos_IF));
  Shifter #(.width(32)) shifter_2 (.in(bit_extender_1_out), .\dist (5'b10000), .out(shifter_2_out));
  Adder #(.width(32)) adder_2 (.a(shifter_1_out), .b(nPC_IF), .out(jmpPC_IF));  // open: cin, cout
  Multiplexer #(.width(32)) multiplexer_3 (.in0(nPC_IF), .in1(jmpPC_IF), .out(Choiced_PC_IF), .sel(Choice_IF));
  CPU_ALU_Control cpu_alu_control_1 (.ALUOp(ALUOp_IF), .fruction(fruc_IF), .Op(InnerOp_IF));
  NEW_IF_UNIT new_if_unit_1 (
    .ins(opcode_IF), .func(fruc_IF), .RegDst(RegDst_IF), .RegWrite(RegWrite_IF), .ALUSrc(ALUSrc_IF),
    .Branch(Branch_IF), .MemRead(MemRead_IF), .MemWrite(MemWrite_IF), .MemReg(MemReg_IF), .ImmPos(ImmPos_IF),
    .ALUOp(ALUOp_IF), .Jcond(Jcond_IF), .STP(STP_IF), .isXor(isXor_IF));
  not not_4 (not_4_out, and_2_out);
  IF_ID if_id_1 (
    .IsXor_in(isXor_IF), .Choice_in(Choice_IF), .nPC_in(nPC_IF), .rs_in(rs_IF), .rt_in(rt_IF),
    .rd_in(rawImm_IF[15:11]), .RegDst_in(RegDst_IF), .rawImm_in({rawImm_IF, fruc_IF}), .ALUSrc_in(ALUSrc_IF),
    .ImmPos_in(ImmPos_IF), .InnerOp_in(InnerOp_IF), .Branch_in(Branch_IF), .MemRead_in(MemRead_IF),
    .MemWrite_in(MemWrite_IF), .Jcond_in(Jcond_IF), .OpMemory_in(1'b1), .OpByte_in(1'b0),
    .MemReg_in(MemReg_IF), .RegWrite_in(RegWrite_IF), .STP_in(STP_IF), .flush(1'b0), .WE(not_4_out),
    .CLK(CLK), .isXor_out(if_id_1_isxor_out), .Choice_out(Pretested_Choice_ID), .nPC_out(if_id_1_npc_out),
    .rs_out(if_id_1_rs_out), .rt_out(if_id_1_rt_out), .rd_out(if_id_1_rd_out),
    .RegDst_out(if_id_1_regdst_out), .rawImm_out(if_id_1_rawimm_out), .ALUSrc_out(if_id_1_alusrc_out),
    .ImmPos_out(if_id_1_immpos_out), .InnerOp_out(if_id_1_innerop_out), .Branch_out(Pretested_Branch_ID),
    .MemRead_out(Pretested_MemRead_ID), .MemWrite_out(Pretested_MemWrite_ID), .Jcond_out(if_id_1_jcond_out),
    .OpMemory_out(if_id_1_opmemory_out), .OpByte_out(if_id_1_opbyte_out), .MemReg_out(if_id_1_memreg_out),
    .RegWrite_out(Pretested_RegWrite_ID), .STP_out(Pretested_STP_ID));
  RiskControlUnit riskcontrolunit_1 (
    .MemRead_EX(id_ex_1_memread_out), .RegWrite_EX(multiplexer_13_out), .rs_ID(if_id_1_rs_out),
    .rt_ID(if_id_1_rt_out), .is_risk(riskcontrolunit_1_is_risk));
  not not_5 (not_5_out, 1'b0);
  not not_6 (not_6_out, xor_2_out);
  Multiplexer multiplexer_4 (.in0(riskcontrolunit_1_is_risk), .in1(1'b0), .out(multiplexer_4_out), .sel(not_5_out));
  and and_2 (and_2_out, not_6_out, multiplexer_4_out);
  or or_1 (or_1_out, xor_2_out, and_2_out);
  Multiplexer multiplexer_5 (.in0(Pretested_Choice_ID), .in1(1'b0), .out(Choice_ID), .sel(or_1_out));
  CPU_RigisterFile cpu_rigisterfile_1 (
    .raddr1(if_id_1_rs_out), .raddr2(if_id_1_rt_out), .waddr(mem_wb_1_regwaddr_out),
    .wdata(mem_wb_1_writebackdate_out), .wen(mem_wb_1_regwrite_out), .CLK(CLK),
    .rdata1(cpu_rigisterfile_1_rdata1), .rdata2(cpu_rigisterfile_1_rdata2));
  Multiplexer multiplexer_6 (.in0(Pretested_MemRead_ID), .in1(1'b0), .out(MemRead_ID), .sel(or_1_out));
  Multiplexer multiplexer_7 (.in0(Pretested_MemWrite_ID), .in1(1'b0), .out(MemWrite_ID), .sel(or_1_out));
  Multiplexer multiplexer_8 (.in0(Pretested_RegWrite_ID), .in1(1'b0), .out(RegWrite_ID), .sel(or_1_out));
  Multiplexer multiplexer_9 (.in0(Pretested_STP_ID), .in1(1'b0), .out(STP_ID), .sel(or_1_out));
  Multiplexer multiplexer_10 (.in0(Pretested_Branch_ID), .in1(1'b0), .out(Branch_ID), .sel(or_1_out));
  ID_EX id_ex_1 (
    .isXor_in(if_id_1_isxor_out), .rdata1_in(cpu_rigisterfile_1_rdata1),
    .rdata2_in(cpu_rigisterfile_1_rdata2), .Choice_in(Choice_ID), .nPC_in(if_id_1_npc_out),
    .rs_in(if_id_1_rs_out), .rt_in(if_id_1_rt_out), .rd_in(if_id_1_rd_out), .RegDst_in(if_id_1_regdst_out),
    .rawImm_in(if_id_1_rawimm_out), .ALUSrc_in(if_id_1_alusrc_out), .ImmPos_in(if_id_1_immpos_out),
    .InnerOp_in(if_id_1_innerop_out), .Branch_in(Branch_ID), .MemRead_in(MemRead_ID),
    .MemWrite_in(MemWrite_ID), .Jcond_in(if_id_1_jcond_out), .OpMemory_in(if_id_1_opmemory_out),
    .OpByte_in(if_id_1_opbyte_out), .MemReg_in(if_id_1_memreg_out), .RegWrite_in(RegWrite_ID),
    .STP_in(STP_ID), .WE(1'b1), .CLK(CLK), .isXor_out(isXor_EX), .rdata1_out(id_ex_1_rdata1_out),
    .rdata2_out(id_ex_1_rdata2_out), .Choice_out(id_ex_1_choice_out), .nPC_out(nPC_EX),
    .rs_out(id_ex_1_rs_out), .rt_out(id_ex_1_rt_out), .rd_out(id_ex_1_rd_out),
    .RegDst_out(id_ex_1_regdst_out), .rawImm_out(rawImm_EX), .ALUSrc_out(ALUSrc_EX), .ImmPos_out(ImmPos_EX),
    .InnerOp_out(id_ex_1_innerop_out), .Branch_out(Branch_EX), .MemRead_out(id_ex_1_memread_out),
    .MemWrite_out(id_ex_1_memwrite_out), .Jcond_out(id_ex_1_jcond_out), .OpMemory_out(id_ex_1_opmemory_out),
    .OpByte_out(id_ex_1_opbyte_out), .MemReg_out(id_ex_1_memreg_out), .RegWrite_out(id_ex_1_regwrite_out),
    .STP_out(id_ex_1_stp_out));
  Multiplexer #(.select(2), .width(32)) multiplexer_11 (
    .in0(id_ex_1_rdata1_out), .in1(mem_wb_1_writebackdate_out), .in2(multiplexer_20_out), .out(OpNum1_EX),
    .sel(ForwardA_EX));  // open: in3
  Multiplexer #(.select(2), .width(32)) multiplexer_12 (
    .in0(id_ex_1_rdata2_out), .in1(mem_wb_1_writebackdate_out), .in2(multiplexer_20_out),
    .out(Pxor_OpNum2_EX), .sel(ForwardB_EX));  // open: in3
  Multiplexer #(.width(5)) multiplexer_13 (
    .in0(id_ex_1_rt_out), .in1(id_ex_1_rd_out), .out(multiplexer_13_out), .sel(id_ex_1_regdst_out));
  Comparator #(.width(32)) comparator_1 (.a(Count), .b(32'h33), .eq(comparator_1_eq));  // open: gt, lt
  Comparator #(.width(32)) comparator_2 (.a(Count), .b(32'h42), .eq(comparator_2_eq));  // open: gt, lt
  Comparator #(.width(32)) comparator_3 (.a(Count), .b(32'ha1), .eq(comparator_3_eq));  // open: gt, lt
  Comparator #(.width(32)) comparator_4 (.a(Count), .b(32'hac), .eq(comparator_4_eq));  // open: gt, lt
  Comparator #(.width(32)) comparator_5 (.a(Count), .b(32'h428), .eq(comparator_5_eq));  // open: gt, lt
  Comparator #(.width(32)) comparator_6 (.a(Count), .b(32'h433), .eq(comparator_6_eq));  // open: gt, lt
  Comparator #(.width(32)) comparator_7 (.a(Count), .b(32'h74b), .eq(comparator_7_eq));  // open: gt, lt
  assign bit_extender_2_out = {{16{rawImm_EX[15]}}, rawImm_EX};  // Bit_Extender bit_extender_2
  Subtractor #(.width(32)) subtractor_1 (.a(nPC_EX), .b(32'h4), .out(PC_EX));  // open: bin, bout
  Shifter #(.width(32)) shifter_3 (.in(bit_extender_2_out), .\dist (5'b10000), .out(shifter_3_out));
  Shifter #(.width(32)) shifter_4 (.in(Imm_EX), .\dist (5'b00010), .out(shifter_4_out));
  assign xor_1_out = 32'hffff ^ Pxor_OpNum2_EX;  // XOR_Gate xor_1, 32 bits wide
  BypassUnit_EX bypassunit_ex_1 (
    .rs(id_ex_1_rs_out), .rt(id_ex_1_rt_out), .RegWrite_EX(ex_mem_1_regwrite_out),
    .waddr_EX(ex_mem_1_regwaddr_out), .RegWrite_WB(mem_wb_1_regwrite_out), .waddr_WB(mem_wb_1_regwaddr_out),
    .ForwardA(ForwardA_EX), .ForwardB(ForwardB_EX));
  or or_2 (or_2_out, comparator_5_eq, comparator_1_eq, comparator_3_eq, comparator_7_eq, comparator_4_eq, comparator_2_eq, comparator_6_eq);
  Multiplexer #(.width(32)) multiplexer_14 (
    .in0(bit_extender_2_out), .in1(shifter_3_out), .out(Imm_EX), .sel(ImmPos_EX));
  Adder #(.width(32)) adder_3 (.a(shifter_4_out), .b(nPC_EX), .out(jmpPC_EX));  // open: cin, cout
  Multiplexer #(.width(32)) multiplexer_15 (.in0(Pxor_OpNum2_EX), .in1(xor_1_out), .out(OpNum2_EX), .sel(isXor_EX));
  Multiplexer #(.width(32)) multiplexer_16 (.in0(OpNum2_EX), .in1(Imm_EX), .out(multiplexer_16_out), .sel(ALUSrc_EX));
  not not_7 (not_7_out, or_2_out);
  not not_8 (not_8_out, CondFit_IF);
  CPU_ALU cpu_alu_1 (
    .OP(id_ex_1_innerop_out), .Input1(OpNum1_EX), .Input2(multiplexer_16_out), .result(cpu_alu_1_result),
    .ZeroFlag(cpu_alu_1_zeroflag));
  Multiplexer multiplexer_17 (.in0(not_8_out), .in1(CondFit_IF), .out(multiplexer_17_out), .sel(not_7_out));
  not not_9 (not_9_out, cpu_alu_1_zeroflag);
  Multiplexer multiplexer_18 (.in0(not_9_out), .in1(cpu_alu_1_zeroflag), .out(CondFit_EX), .sel(id_ex_1_jcond_out));
  and and_3 (Choice_IF, multiplexer_17_out, Branch_IF);
  Multiplexer #(.width(32)) multiplexer_19 (.in0(nPC_EX), .in1(jmpPC_EX), .out(multiplexer_19_out), .sel(and_4_out));
  and and_4 (and_4_out, CondFit_EX, Branch_EX);
  EX_MEM ex_mem_1 (
    .res_in(cpu_alu_1_result), .MemRead_in(id_ex_1_memread_out), .MemWrite_in(id_ex_1_memwrite_out),
    .Regwaddr_in(multiplexer_13_out), .OpMemory_in(id_ex_1_opmemory_out), .OpByte_in(id_ex_1_opbyte_out),
    .MemReg_in(id_ex_1_memreg_out), .RegWrite_in(id_ex_1_regwrite_out), .STP_in(id_ex_1_stp_out),
    .MemWriteData_in(OpNum2_EX), .WE(1'b1), .CLK(CLK), .res_out(ex_mem_1_res_out),
    .MemRead_out(ex_mem_1_memread_out), .MemWrite_out(ex_mem_1_memwrite_out),
    .Regwaddr_out(ex_mem_1_regwaddr_out), .OpMemory_out(ex_mem_1_opmemory_out),
    .OpByte_out(ex_mem_1_opbyte_out), .MemReg_out(ex_mem_1_memreg_out), .RegWrite_out(ex_mem_1_regwrite_out),
    .STP_out(ex_mem_1_stp_out), .MemWriteData_out(ex_mem_1_memwritedata_out));
  xor xor_2 (xor_2_out, and_4_out, id_ex_1_choice_out);
  Counter #(.max('hf), .width(4)) counter_2 (.load(1'b0), .count(xor_2_out), .clk(CLK));  // open: clr, up, D, carry, Q
  USED_RAM used_ram_1 (
    .OpMemory(ex_mem_1_opmemory_out), .WriteEnable(ex_mem_1_memwrite_out), .ReadEnable(ex_mem_1_memread_out),
    .OpByte(ex_mem_1_opbyte_out), .addr(ex_mem_1_res_out), .datain(ex_mem_1_memwritedata_out), .CLK(CLK),
    .dataout(used_ram_1_dataout));  // open: addr_illegal
  Multiplexer #(.width(32)) multiplexer_20 (
    .in0(used_ram_1_dataout), .in1(ex_mem_1_res_out), .out(multiplexer_20_out), .sel(ex_mem_1_memreg_out));
  MEM_WB mem_wb_1 (
    .WriteBackData_in(multiplexer_20_out), .Regwaddr_in(ex_mem_1_regwaddr_out),
    .RegWrite_in(ex_mem_1_regwrite_out), .STP_in(ex_mem_1_stp_out), .WE(1'b1), .CLK(CLK),
    .WriteBackDate_out(mem_wb_1_writebackdate_out), .Regwaddr_out(mem_wb_1_regwaddr_out),
    .RegWrite_out(mem_wb_1_regwrite_out), .STP_out(STP));

  // Other names for the same wires on the sheet: rawImm_IF[5:0] = fruc_IF; sa_IF[4:0] = rawImm_IF[10:6];
  //   rd_IF[4:0] = rawImm_IF[15:11]

  // Notes on the sheet:
  //   Dont change it to 1
  //   T_COUNT
  //   contents of rom_1 (hex, n*v repeats v):
  //   4021 9821 8e09000c 8d100000 8e110000 8e320000 8e530000 1669fff8 2777821 36f80050 34190054 3c0d7f38
  //   35add3c9 3c0e7f38 35ced3c5 1ae2022 8def0000 adef0000 1e47821 15e4fffc 2114021 2534821 1099021
  //   ae320000 8e320000 2518822 ae110000 3c140000 36f40014 36eb0001 2108021 ac300000 8c300000 28ba022
  //   1680fffb 34140064 af110000 af330000 8f110000 8f330000 2339827 af330000 320c021 99c821 28ba022
  //   1694ffd2 16f4fff7 34140064 af110000 af330000 8f110000 8f330000 2339823 af330000 320c021 99c821
  //   28ba022 16f4fff8 3c106799 36100cb8 34110010 ae300000 fc000000
  //   No wire go through StatusRigister by tunnel,which is just used in a single realm
  //   opcode
  //   IF
  //   GK's CPU
  //   ID
  //   EX(the only one who without CLK!!!)
  //   rt--(alu/not)-->midres--(*p/not)-->final
  //   imm--(alu)-->midres--(*p/not)-->final
  //   MEM
  //   WB
endmodule

module CPU_RigisterFile (
  input  [4:0] raddr1,
  input  [4:0] raddr2,
  input  [4:0] waddr,
  input  [31:0] wdata,
  input  wen,
  input  CLK,
  output [31:0] rdata1,
  output [31:0] rdata2
);

  wire demultiplexer_1_out0, demultiplexer_1_out1, demultiplexer_1_out2, demultiplexer_1_out3;
  wire [31:0] cpu_rigisterfile_8_1_rdata1, cpu_rigisterfile_8_1_rdata2, cpu_rigisterfile_8_2_rdata1,
       cpu_rigisterfile_8_2_rdata2, cpu_rigisterfile_8_3_rdata1, cpu_rigisterfile_8_3_rdata2,
       cpu_rigisterfile_8_4_rdata1, cpu_rigisterfile_8_4_rdata2;

  Demultiplexer #(.select(2)) demultiplexer_1 (
    .out0(demultiplexer_1_out0), .out1(demultiplexer_1_out1), .out2(demultiplexer_1_out2),
    .out3(demultiplexer_1_out3), .in(wen), .sel(waddr[4:3]));
  CPU_RigisterFile_8 cpu_rigisterfile_8_1 (
    .wen(demultiplexer_1_out0), .wdata(wdata), .waddr(waddr[2:0]), .CLK(CLK), .raddr1(raddr1[2:0]),
    .raddr2(raddr2[2:0]), .rdata1(cpu_rigisterfile_8_1_rdata1), .rdata2(cpu_rigisterfile_8_1_rdata2));
  CPU_RigisterFile_8 cpu_rigisterfile_8_2 (
    .wen(demultiplexer_1_out1), .wdata(wdata), .waddr(waddr[2:0]), .CLK(CLK), .raddr1(raddr1[2:0]),
    .raddr2(raddr2[2:0]), .rdata1(cpu_rigisterfile_8_2_rdata1), .rdata2(cpu_rigisterfile_8_2_rdata2));
  CPU_RigisterFile_8 cpu_rigisterfile_8_3 (
    .wen(demultiplexer_1_out2), .wdata(wdata), .waddr(waddr[2:0]), .CLK(CLK), .raddr1(raddr1[2:0]),
    .raddr2(raddr2[2:0]), .rdata1(cpu_rigisterfile_8_3_rdata1), .rdata2(cpu_rigisterfile_8_3_rdata2));
  CPU_RigisterFile_8 cpu_rigisterfile_8_4 (
    .wen(demultiplexer_1_out3), .wdata(wdata), .waddr(waddr[2:0]), .CLK(CLK), .raddr1(raddr1[2:0]),
    .raddr2(raddr2[2:0]), .rdata1(cpu_rigisterfile_8_4_rdata1), .rdata2(cpu_rigisterfile_8_4_rdata2));
  Multiplexer #(.select(2), .width(32)) multiplexer_1 (
    .in0(cpu_rigisterfile_8_1_rdata1), .in1(cpu_rigisterfile_8_2_rdata1), .in2(cpu_rigisterfile_8_3_rdata1),
    .in3(cpu_rigisterfile_8_4_rdata1), .out(rdata1), .sel(raddr1[4:3]));
  Multiplexer #(.select(2), .width(32)) multiplexer_2 (
    .in0(cpu_rigisterfile_8_1_rdata2), .in1(cpu_rigisterfile_8_2_rdata2), .in2(cpu_rigisterfile_8_3_rdata2),
    .in3(cpu_rigisterfile_8_4_rdata2), .out(rdata2), .sel(raddr2[4:3]));

  // Notes on the sheet:
  //   wen: initial=0x1
endmodule

module CPU_RigisterFile_8 (
  input  wen,
  input  [31:0] wdata,
  input  [2:0] waddr,
  input  CLK,
  input  [2:0] raddr1,
  input  [2:0] raddr2,
  output [31:0] rdata1,
  output [31:0] rdata2
);

  wire and_1_out, and_2_out, comparator_1_eq, comparator_2_eq, demultiplexer_1_out0, demultiplexer_1_out1,
       demultiplexer_1_out2, demultiplexer_1_out3, demultiplexer_1_out4, demultiplexer_1_out5,
       demultiplexer_1_out6, demultiplexer_1_out7;
  wire [31:0] multiplexer_1_out, multiplexer_2_out, register_1_q, register_2_q, register_3_q, register_4_q,
       register_5_q, register_6_q, register_7_q, register_8_q;

  Register #(.width(32)) register_1 (.D(wdata), .en(demultiplexer_1_out0), .clk(CLK), .Q(register_1_q));  // open: clr
  Register #(.width(32)) register_2 (.D(wdata), .en(demultiplexer_1_out2), .clk(CLK), .Q(register_2_q));  // open: clr
  Register #(.width(32)) register_3 (.D(wdata), .en(demultiplexer_1_out4), .clk(CLK), .Q(register_3_q));  // open: clr
  Register #(.width(32)) register_4 (.D(wdata), .en(demultiplexer_1_out6), .clk(CLK), .Q(register_4_q));  // open: clr
  Demultiplexer #(.select(3)) demultiplexer_1 (
    .out0(demultiplexer_1_out0), .out1(demultiplexer_1_out1), .out2(demultiplexer_1_out2),
    .out3(demultiplexer_1_out3), .out4(demultiplexer_1_out4), .out5(demultiplexer_1_out5),
    .out6(demultiplexer_1_out6), .out7(demultiplexer_1_out7), .in(wen), .sel(waddr));
  Register #(.width(32)) register_5 (.D(wdata), .en(demultiplexer_1_out1), .clk(CLK), .Q(register_5_q));  // open: clr
  Register #(.width(32)) register_6 (.D(wdata), .en(demultiplexer_1_out3), .clk(CLK), .Q(register_6_q));  // open: clr
  Register #(.width(32)) register_7 (.D(wdata), .en(demultiplexer_1_out5), .clk(CLK), .Q(register_7_q));  // open: clr
  Register #(.width(32)) register_8 (.D(wdata), .en(demultiplexer_1_out7), .clk(CLK), .Q(register_8_q));  // open: clr
  Multiplexer #(.select(3), .width(32)) multiplexer_1 (
    .in0(register_1_q), .in1(register_5_q), .in2(register_2_q), .in3(register_6_q), .in4(register_3_q),
    .in5(register_7_q), .in6(register_4_q), .in7(register_8_q), .out(multiplexer_1_out), .sel(raddr1));
  Multiplexer #(.select(3), .width(32)) multiplexer_2 (
    .in0(register_1_q), .in1(register_5_q), .in2(register_2_q), .in3(register_6_q), .in4(register_3_q),
    .in5(register_7_q), .in6(register_4_q), .in7(register_8_q), .out(multiplexer_2_out), .sel(raddr2));
  Comparator #(.mode("unsigned"), .width(3)) comparator_1 (
    .a(raddr1), .b(waddr), .eq(comparator_1_eq));  // open: gt, lt
  Comparator #(.mode("unsigned"), .width(3)) comparator_2 (
    .a(raddr2), .b(waddr), .eq(comparator_2_eq));  // open: gt, lt
  // Probe on register_1_q
  // Probe on register_5_q
  // Probe on register_2_q
  // Probe on register_6_q
  // Probe on register_3_q
  // Probe on register_7_q
  // Probe on register_4_q
  // Probe on register_8_q
  and and_1 (and_1_out, comparator_1_eq, wen);
  and and_2 (and_2_out, comparator_2_eq, wen);
  Multiplexer #(.width(32)) multiplexer_3 (.in0(multiplexer_1_out), .in1(wdata), .out(rdata1), .sel(and_1_out));
  Multiplexer #(.width(32)) multiplexer_4 (.in0(multiplexer_2_out), .in1(wdata), .out(rdata2), .sel(and_2_out));

  // Notes on the sheet:
  //   wen: initial=0x1
endmodule

module CPU_ALU (
  input  [3:0] OP,
  input  [31:0] Input1,
  input  [31:0] Input2,
  output [31:0] result,
  output ZeroFlag
);

  wire [4:0] bit_extender_1_out, bit_extender_2_out, bit_extender_3_out;
  wire [31:0] adder_1_out, adder_2_out, divider_1_out, fpadder_1_out, fpdivider_1_out, fpmultiplier_1_out,
       fpsubtractor_1_out, fptoint_1_p2, inttofp_1_p4, multiplier_1_out, not_1_out, or_1_out, shifter_1_out,
       shifter_2_out, shifter_3_out, subtractor_1_out, xor_1_out, xor_2_out;

  Bit_Extender #(.in_width(32), .out_width(5), .\type ("zero")) bit_extender_1 (.in(Input2), .out(bit_extender_1_out));
  Bit_Extender #(.in_width(32), .out_width(5), .\type ("zero")) bit_extender_2 (.in(Input2), .out(bit_extender_2_out));
  Bit_Extender #(.in_width(32), .out_width(5), .\type ("zero")) bit_extender_3 (.in(Input2), .out(bit_extender_3_out));
  Adder #(.width(32)) adder_1 (.a(Input1), .b(Input2), .out(adder_1_out));  // open: cin, cout
  Subtractor #(.width(32)) subtractor_1 (.a(Input1), .b(Input2), .out(subtractor_1_out));  // open: bin, bout
  Multiplier #(.width(32)) multiplier_1 (.a(Input1), .b(Input2), .out(multiplier_1_out));  // open: cin, cout
  Divider #(.width(32)) divider_1 (.a(Input1), .b(Input2), .out(divider_1_out));  // open: upper, rem
  Shifter #(.width(32)) shifter_1 (.in(Input1), .\dist (bit_extender_1_out), .out(shifter_1_out));
  assign or_1_out = Input1 | Input2;  // OR_Gate or_1, 32 bits wide
  assign xor_1_out = 32'hffff ^ Input1;  // XOR_Gate xor_1, 32 bits wide
  assign xor_2_out = Input2 ^ 32'hffff;  // XOR_Gate xor_2, 32 bits wide
  Shifter #(.shift("lr"), .width(32)) shifter_2 (.in(Input1), .\dist (bit_extender_2_out), .out(shifter_2_out));
  Shifter #(.shift("ar"), .width(32)) shifter_3 (.in(Input1), .\dist (bit_extender_3_out), .out(shifter_3_out));
  assign not_1_out = ~Input1;  // NOT_Gate not_1, 32 bits wide
  // IntToFP #(.width(32)) inttofp_1: pin names not known; wires that end beside it: Input1, shifter_2_out, shifter_3_out, inttofp_1_p4
  // FPToInt #(.width(32)) fptoint_1: pin names not known; wires that end beside it: Input1, fptoint_1_p2
  FPAdder fpadder_1 (.a(Input1), .b(Input2), .out(fpadder_1_out));
  FPSubtractor fpsubtractor_1 (.a(Input1), .b(Input2), .out(fpsubtractor_1_out));
  FPMultiplier fpmultiplier_1 (.a(Input1), .b(Input2), .out(fpmultiplier_1_out));
  FPDivider fpdivider_1 (.a(Input1), .b(Input2), .out(fpdivider_1_out));
  Adder #(.width(32)) adder_2 (.a(xor_1_out), .b(xor_2_out), .out(adder_2_out));  // open: cin, cout
  Multiplexer #(.select(4), .width(32)) multiplexer_1 (
    .in0(adder_1_out), .in1(subtractor_1_out), .in2(multiplier_1_out), .in3(divider_1_out),
    .in4(shifter_1_out), .in5(or_1_out), .in6(adder_2_out), .in7(shifter_2_out), .in8(shifter_3_out),
    .in9(not_1_out), .in10(inttofp_1_p4), .in11(fptoint_1_p2), .in12(fpadder_1_out),
    .in13(fpsubtractor_1_out), .in14(fpmultiplier_1_out), .in15(fpdivider_1_out), .out(result), .sel(OP));
  Comparator #(.mode("unsigned"), .width(32)) comparator_1 (.a(result), .b({32{1'b0}}), .eq(ZeroFlag));  // open: gt, lt
endmodule

module CPU_RAM_18 (
  input  OpMemory,
  input  WriteEnable,
  input  ReadEnable,
  input  CLK,
  input  [17:0] addr,
  input  [31:0] datain,
  input  OpByte,
  output [31:0] dataout
);

  wire and_1_out, and_2_out;
  wire [7:0] bit_extender_1_out, multiplexer_3_out;
  wire [31:0] bit_extender_2_out, multiplexer_1_out, multiplexer_2_out, ram_1_dout;

  Bit_Extender #(.in_width(32), .out_width(8)) bit_extender_1 (.in(datain), .out(bit_extender_1_out));
  and and_1 (and_1_out, OpMemory, WriteEnable);
  and and_2 (and_2_out, OpMemory, ReadEnable);
  Multiplexer #(.select(2), .width(32)) multiplexer_1 (
    .in0({ram_1_dout[31:8], bit_extender_1_out}),
    .in1({ram_1_dout[31:16], bit_extender_1_out, ram_1_dout[7:0]}),
    .in2({ram_1_dout[31:24], bit_extender_1_out, ram_1_dout[15:0]}),
    .in3({bit_extender_1_out, ram_1_dout[23:0]}), .out(multiplexer_1_out), .sel(addr[1:0]));
  Multiplexer #(.width(32)) multiplexer_2 (
    .in0(datain), .in1(multiplexer_1_out), .out(multiplexer_2_out), .sel(OpByte));
  RAM #(.addrWidth(16), .asyncread("true"), .dataWidth(32)) ram_1 (
    .addr(addr[17:2]), .we(and_1_out), .oe(and_2_out), .clk(CLK), .din(multiplexer_2_out), .dout(ram_1_dout));
  Multiplexer #(.select(2), .width(8)) multiplexer_3 (
    .in0(ram_1_dout[7:0]), .in1(ram_1_dout[15:8]), .in2(ram_1_dout[23:16]), .in3(ram_1_dout[31:24]),
    .out(multiplexer_3_out), .sel(addr[1:0]));
  assign bit_extender_2_out = {{24{1'b0}}, multiplexer_3_out};  // Bit_Extender bit_extender_2
  Multiplexer #(.width(32)) multiplexer_4 (.in0(ram_1_dout), .in1(bit_extender_2_out), .out(dataout), .sel(OpByte));
  // Probe on dataout

  // Notes on the sheet:
  //   addr: initial=0xfffff
endmodule

module CPU_RAM_20 (
  input  OpMemory,
  input  WriteEnable,
  input  ReadEnable,
  input  OpByte,
  input  [19:0] addr,
  input  [31:0] datain,
  input  CLK,
  output [31:0] dataout
);

  wire and_1_out, and_2_out, and_3_out, and_4_out, decoder_1_out0, decoder_1_out1, decoder_1_out2,
       decoder_1_out3;
  wire [31:0] cpu_ram_18_1_dataout, cpu_ram_18_2_dataout, cpu_ram_18_3_dataout, cpu_ram_18_4_dataout;

  Decoder #(.select(2)) decoder_1 (
    .out0(decoder_1_out0), .out1(decoder_1_out1), .out2(decoder_1_out2), .out3(decoder_1_out3),
    .sel(addr[19:18]));  // open: en
  and and_1 (and_1_out, OpMemory, decoder_1_out0);
  and and_2 (and_2_out, OpMemory, decoder_1_out1);
  and and_3 (and_3_out, OpMemory, decoder_1_out2);
  and and_4 (and_4_out, OpMemory, decoder_1_out3);
  CPU_RAM_18 cpu_ram_18_1 (
    .OpMemory(and_1_out), .WriteEnable(WriteEnable), .ReadEnable(ReadEnable), .CLK(CLK), .addr(addr[17:0]),
    .datain(datain), .OpByte(OpByte), .dataout(cpu_ram_18_1_dataout));
  CPU_RAM_18 cpu_ram_18_2 (
    .OpMemory(and_2_out), .WriteEnable(WriteEnable), .ReadEnable(ReadEnable), .CLK(CLK), .addr(addr[17:0]),
    .datain(datain), .OpByte(OpByte), .dataout(cpu_ram_18_2_dataout));
  CPU_RAM_18 cpu_ram_18_3 (
    .OpMemory(and_3_out), .WriteEnable(WriteEnable), .ReadEnable(ReadEnable), .CLK(CLK), .addr(addr[17:0]),
    .datain(datain), .OpByte(OpByte), .dataout(cpu_ram_18_3_dataout));
  CPU_RAM_18 cpu_ram_18_4 (
    .OpMemory(and_4_out), .WriteEnable(WriteEnable), .ReadEnable(ReadEnable), .CLK(CLK), .addr(addr[17:0]),
    .datain(datain), .OpByte(OpByte), .dataout(cpu_ram_18_4_dataout));
  Multiplexer #(.select(2), .width(32)) multiplexer_1 (
    .in0(cpu_ram_18_1_dataout), .in1(cpu_ram_18_2_dataout), .in2(cpu_ram_18_3_dataout),
    .in3(cpu_ram_18_4_dataout), .out(dataout), .sel(addr[19:18]));

  // Notes on the sheet:
  //   addr: initial=0xfffff
endmodule

module CPU_RAM_22 (
  input  OpMemory,
  input  WriteEnable,
  input  ReadEnable,
  input  OpByte,
  input  [21:0] addr,
  input  [31:0] datain,
  input  CLK,
  output [31:0] dataout
);

  wire and_1_out, and_2_out, and_3_out, and_4_out, decoder_1_out0, decoder_1_out1, decoder_1_out2,
       decoder_1_out3;
  wire [31:0] cpu_ram_20_1_dataout, cpu_ram_20_2_dataout, cpu_ram_20_3_dataout, cpu_ram_20_4_dataout;

  Decoder #(.select(2)) decoder_1 (
    .out0(decoder_1_out0), .out1(decoder_1_out1), .out2(decoder_1_out2), .out3(decoder_1_out3),
    .sel(addr[1:0]));  // open: en
  and and_1 (and_1_out, OpMemory, decoder_1_out0);
  and and_2 (and_2_out, OpMemory, decoder_1_out1);
  and and_3 (and_3_out, OpMemory, decoder_1_out2);
  and and_4 (and_4_out, OpMemory, decoder_1_out3);
  CPU_RAM_20 cpu_ram_20_1 (
    .OpMemory(and_1_out), .WriteEnable(WriteEnable), .ReadEnable(ReadEnable), .OpByte(CLK),
    .addr(addr[21:2]), .datain(datain), .CLK(OpByte), .dataout(cpu_ram_20_1_dataout));
  CPU_RAM_20 cpu_ram_20_2 (
    .OpMemory(and_2_out), .WriteEnable(WriteEnable), .ReadEnable(ReadEnable), .OpByte(CLK),
    .addr(addr[21:2]), .datain(datain), .CLK(OpByte), .dataout(cpu_ram_20_2_dataout));
  CPU_RAM_20 cpu_ram_20_3 (
    .OpMemory(and_3_out), .WriteEnable(WriteEnable), .ReadEnable(ReadEnable), .OpByte(CLK),
    .addr(addr[21:2]), .datain(datain), .CLK(OpByte), .dataout(cpu_ram_20_3_dataout));
  CPU_RAM_20 cpu_ram_20_4 (
    .OpMemory(and_4_out), .WriteEnable(WriteEnable), .ReadEnable(ReadEnable), .OpByte(CLK),
    .addr(addr[21:2]), .datain(datain), .CLK(OpByte), .dataout(cpu_ram_20_4_dataout));
  Multiplexer #(.select(2), .width(32)) multiplexer_1 (
    .in0(cpu_ram_20_1_dataout), .in1(cpu_ram_20_2_dataout), .in2(cpu_ram_20_3_dataout),
    .in3(cpu_ram_20_4_dataout), .out(dataout), .sel(addr[1:0]));

  // Notes on the sheet:
  //   addr: initial=0xfffff
endmodule

module CPU_RAM_24 (
  input  OpMemory,
  input  WriteEnable,
  input  ReadEnable,
  input  OpByte,
  input  [23:0] addr,
  input  [31:0] datain,
  input  CLK,
  output [31:0] dataout
);

  wire and_1_out, and_2_out, and_3_out, and_4_out, decoder_1_out0, decoder_1_out1, decoder_1_out2,
       decoder_1_out3;
  wire [31:0] cpu_ram_22_1_dataout, cpu_ram_22_2_dataout, cpu_ram_22_3_dataout, cpu_ram_22_4_dataout;

  Decoder #(.select(2)) decoder_1 (
    .out0(decoder_1_out0), .out1(decoder_1_out1), .out2(decoder_1_out2), .out3(decoder_1_out3),
    .sel(addr[1:0]));  // open: en
  and and_1 (and_1_out, OpMemory, decoder_1_out0);
  and and_2 (and_2_out, OpMemory, decoder_1_out1);
  and and_3 (and_3_out, OpMemory, decoder_1_out2);
  and and_4 (and_4_out, OpMemory, decoder_1_out3);
  CPU_RAM_22 cpu_ram_22_1 (
    .OpMemory(and_1_out), .WriteEnable(WriteEnable), .ReadEnable(ReadEnable), .OpByte(CLK),
    .addr(addr[23:2]), .datain(datain), .CLK(OpByte), .dataout(cpu_ram_22_1_dataout));
  CPU_RAM_22 cpu_ram_22_2 (
    .OpMemory(and_2_out), .WriteEnable(WriteEnable), .ReadEnable(ReadEnable), .OpByte(CLK),
    .addr(addr[23:2]), .datain(datain), .CLK(OpByte), .dataout(cpu_ram_22_2_dataout));
  CPU_RAM_22 cpu_ram_22_3 (
    .OpMemory(and_3_out), .WriteEnable(WriteEnable), .ReadEnable(ReadEnable), .OpByte(CLK),
    .addr(addr[23:2]), .datain(datain), .CLK(OpByte), .dataout(cpu_ram_22_3_dataout));
  CPU_RAM_22 cpu_ram_22_4 (
    .OpMemory(and_4_out), .WriteEnable(WriteEnable), .ReadEnable(ReadEnable), .OpByte(CLK),
    .addr(addr[23:2]), .datain(datain), .CLK(OpByte), .dataout(cpu_ram_22_4_dataout));
  Multiplexer #(.select(2), .width(32)) multiplexer_1 (
    .in0(cpu_ram_22_1_dataout), .in1(cpu_ram_22_2_dataout), .in2(cpu_ram_22_3_dataout),
    .in3(cpu_ram_22_4_dataout), .out(dataout), .sel(addr[1:0]));

  // Notes on the sheet:
  //   addr: initial=0xfffff
endmodule

module CPU_RAM_26 (
  input  OpMemory,
  input  WriteEnable,
  input  ReadEnable,
  input  OpByte,
  input  [25:0] addr,
  input  [31:0] datain,
  input  CLK,
  output [31:0] dataout
);

  wire and_1_out, and_2_out, and_3_out, and_4_out, decoder_1_out0, decoder_1_out1, decoder_1_out2,
       decoder_1_out3;
  wire [31:0] cpu_ram_24_1_dataout, cpu_ram_24_2_dataout, cpu_ram_24_3_dataout, cpu_ram_24_4_dataout;

  Decoder #(.select(2)) decoder_1 (
    .out0(decoder_1_out0), .out1(decoder_1_out1), .out2(decoder_1_out2), .out3(decoder_1_out3),
    .sel(addr[1:0]));  // open: en
  and and_1 (and_1_out, OpMemory, decoder_1_out0);
  and and_2 (and_2_out, OpMemory, decoder_1_out1);
  and and_3 (and_3_out, OpMemory, decoder_1_out2);
  and and_4 (and_4_out, OpMemory, decoder_1_out3);
  CPU_RAM_24 cpu_ram_24_1 (
    .OpMemory(and_1_out), .WriteEnable(WriteEnable), .ReadEnable(ReadEnable), .OpByte(CLK),
    .addr(addr[25:2]), .datain(datain), .CLK(OpByte), .dataout(cpu_ram_24_1_dataout));
  CPU_RAM_24 cpu_ram_24_2 (
    .OpMemory(and_2_out), .WriteEnable(WriteEnable), .ReadEnable(ReadEnable), .OpByte(CLK),
    .addr(addr[25:2]), .datain(datain), .CLK(OpByte), .dataout(cpu_ram_24_2_dataout));
  CPU_RAM_24 cpu_ram_24_3 (
    .OpMemory(and_3_out), .WriteEnable(WriteEnable), .ReadEnable(ReadEnable), .OpByte(CLK),
    .addr(addr[25:2]), .datain(datain), .CLK(OpByte), .dataout(cpu_ram_24_3_dataout));
  CPU_RAM_24 cpu_ram_24_4 (
    .OpMemory(and_4_out), .WriteEnable(WriteEnable), .ReadEnable(ReadEnable), .OpByte(CLK),
    .addr(addr[25:2]), .datain(datain), .CLK(OpByte), .dataout(cpu_ram_24_4_dataout));
  Multiplexer #(.select(2), .width(32)) multiplexer_1 (
    .in0(cpu_ram_24_1_dataout), .in1(cpu_ram_24_2_dataout), .in2(cpu_ram_24_3_dataout),
    .in3(cpu_ram_24_4_dataout), .out(dataout), .sel(addr[1:0]));

  // Notes on the sheet:
  //   addr: initial=0xfffff
endmodule

module CPU_RAM_28 (
  input  OpMemory,
  input  WriteEnable,
  input  ReadEnable,
  input  OpByte,
  input  [27:0] addr,
  input  [31:0] datain,
  input  CLK,
  output [31:0] dataout
);

  wire and_1_out, and_2_out, and_3_out, and_4_out, decoder_1_out0, decoder_1_out1, decoder_1_out2,
       decoder_1_out3;
  wire [31:0] cpu_ram_26_1_dataout, cpu_ram_26_2_dataout, cpu_ram_26_3_dataout, cpu_ram_26_4_dataout;

  Decoder #(.select(2)) decoder_1 (
    .out0(decoder_1_out0), .out1(decoder_1_out1), .out2(decoder_1_out2), .out3(decoder_1_out3),
    .sel(addr[1:0]));  // open: en
  and and_1 (and_1_out, OpMemory, decoder_1_out0);
  and and_2 (and_2_out, OpMemory, decoder_1_out1);
  and and_3 (and_3_out, OpMemory, decoder_1_out2);
  and and_4 (and_4_out, OpMemory, decoder_1_out3);
  CPU_RAM_26 cpu_ram_26_1 (
    .OpMemory(and_1_out), .WriteEnable(WriteEnable), .ReadEnable(ReadEnable), .OpByte(CLK),
    .addr(addr[27:2]), .datain(datain), .CLK(OpByte), .dataout(cpu_ram_26_1_dataout));
  CPU_RAM_26 cpu_ram_26_2 (
    .OpMemory(and_2_out), .WriteEnable(WriteEnable), .ReadEnable(ReadEnable), .OpByte(CLK),
    .addr(addr[27:2]), .datain(datain), .CLK(OpByte), .dataout(cpu_ram_26_2_dataout));
  CPU_RAM_26 cpu_ram_26_3 (
    .OpMemory(and_3_out), .WriteEnable(WriteEnable), .ReadEnable(ReadEnable), .OpByte(CLK),
    .addr(addr[27:2]), .datain(datain), .CLK(OpByte), .dataout(cpu_ram_26_3_dataout));
  CPU_RAM_26 cpu_ram_26_4 (
    .OpMemory(and_4_out), .WriteEnable(WriteEnable), .ReadEnable(ReadEnable), .OpByte(CLK),
    .addr(addr[27:2]), .datain(datain), .CLK(OpByte), .dataout(cpu_ram_26_4_dataout));
  Multiplexer #(.select(2), .width(32)) multiplexer_1 (
    .in0(cpu_ram_26_1_dataout), .in1(cpu_ram_26_2_dataout), .in2(cpu_ram_26_3_dataout),
    .in3(cpu_ram_26_4_dataout), .out(dataout), .sel(addr[1:0]));

  // Notes on the sheet:
  //   addr: initial=0xfffff
endmodule

module CPU_RAM (
  input  OpMemory,
  input  WriteEnable,
  input  ReadEnable,
  input  OpByte,
  input  [31:0] addr,
  input  [31:0] datain,
  input  CLK,
  output [31:0] dataout,
  output addr_illegal
);

  wire comparator_1_eq;
  wire [23:0] bit_extender_1_out;

  Bit_Extender #(.in_width(32), .out_width(24)) bit_extender_1 (.in(addr), .out(bit_extender_1_out));
  CPU_RAM_24 cpu_ram_24_1 (
    .OpMemory(OpMemory), .WriteEnable(WriteEnable), .ReadEnable(ReadEnable), .OpByte(OpByte),
    .addr(bit_extender_1_out), .datain(datain), .CLK(CLK), .dataout(dataout));
  Comparator #(.mode("unsigned")) comparator_1 (.a(addr[31:24]), .b({8{1'b0}}), .eq(comparator_1_eq));  // open: gt, lt
  not not_1 (addr_illegal, comparator_1_eq);

  // Notes on the sheet:
  //   addr: initial=0xfffff
endmodule

module CPU_ALU_Control (
  input  [2:0] ALUOp,
  input  [5:0] fruction,
  output [3:0] Op
);

  wire [3:0] bit_extender_1_out, subtractor_1_out;

  Bit_Extender #(.in_width(6), .out_width(4)) bit_extender_1 (.in(fruction), .out(bit_extender_1_out));
  Subtractor #(.width(4)) subtractor_1 (
    .a(bit_extender_1_out), .b(4'b0001), .out(subtractor_1_out));  // open: bin, bout
  Multiplexer #(.select(3), .width(4)) multiplexer_1 (
    .in0(4'b0000), .in1(4'b0001), .in2(4'b0010), .in3(4'b0011), .in4(4'b0100), .in5(4'b0101), .in6(4'b0110),
    .in7(subtractor_1_out), .out(Op), .sel(ALUOp));
endmodule

module CPU_INS_Control (
  input  [5:0] ins,
  output RegDst,
  output RegWrite,
  output ALUSrc,
  output Branch,
  output MemRead,
  output MemWrite,
  output MemReg,
  output ImmPos,
  output [2:0] ALUOp,
  output Jcond,
  output STP
);

  ControlUnit controlunit_1 (
    .ControlCode(ins), .RegDst(RegDst), .RegWrite(RegWrite), .ALUSrc(ALUSrc), .Branch(Branch),
    .MemRead(MemRead), .MemWrite(MemWrite), .MemtoReg(MemReg), .ImmPos(ImmPos), .ALUop(ALUOp), .JCond(Jcond),
    .STP(STP));
endmodule

module ControlUnit (
  input  [5:0] ControlCode,
  output RegDst,
  output RegWrite,
  output ALUSrc,
  output Branch,
  output MemRead,
  output MemWrite,
  output MemtoReg,
  output ImmPos,
  output [2:0] ALUop,
  output JCond,
  output STP
);

  wire and_1_out, and_2_out, and_3_out, and_4_out, and_5_out, and_6_out, and_10_out, and_12_out, and_13_out,
       and_14_out, and_15_out, and_16_out, and_17_out, not_1_out, not_2_out, not_3_out, not_4_out, not_5_out,
       not_6_out;

  not not_1 (not_1_out, ControlCode[5]);
  not not_2 (not_2_out, ControlCode[4]);
  not not_3 (not_3_out, ControlCode[3]);
  not not_4 (not_4_out, ControlCode[2]);
  not not_5 (not_5_out, ControlCode[1]);
  not not_6 (not_6_out, ControlCode[0]);
  and and_1 (and_1_out, not_4_out, not_5_out);
  or or_1 (RegDst, and_1_out, and_2_out);
  and and_2 (and_2_out, ControlCode[4], not_5_out);
  and and_3 (and_3_out, not_3_out, not_4_out);
  or or_2 (RegWrite, and_3_out, and_4_out);
  and and_4 (and_4_out, not_1_out, ControlCode[3]);
  and and_5 (and_5_out, not_2_out, ControlCode[1]);
  or or_3 (ALUSrc, and_5_out, and_6_out);
  and and_6 (and_6_out, not_2_out, ControlCode[3], ControlCode[2]);
  and and_7 (Branch, not_3_out, ControlCode[2]);
  and and_8 (MemRead, not_3_out, ControlCode[1]);
  and and_9 (MemWrite, ControlCode[3], not_4_out, ControlCode[1]);
  or or_4 (MemtoReg, not_1_out, and_10_out);
  and and_10 (and_10_out, not_2_out, ControlCode[3]);
  and and_11 (ImmPos, not_1_out, ControlCode[1]);
  and and_12 (and_12_out, ControlCode[3], not_5_out);
  or or_5 (ALUop[2], and_12_out, and_13_out);
  and and_13 (and_13_out, not_4_out, not_5_out);
  and and_14 (and_14_out, ControlCode[3], not_5_out);
  or or_6 (ALUop[1], and_14_out, and_15_out);
  and and_15 (and_15_out, not_4_out, not_5_out);
  and and_16 (and_16_out, not_3_out, not_5_out);
  or or_7 (ALUop[0], not_6_out, and_16_out, and_17_out);
  and and_17 (and_17_out, not_1_out, not_4_out);
  and and_18 (JCond, not_3_out, ControlCode[2], not_6_out);
  and and_19 (STP, ControlCode[4], ControlCode[0]);
endmodule

module USED_RAM (
  input  OpMemory,
  input  WriteEnable,
  input  ReadEnable,
  input  OpByte,
  input  [31:0] addr,
  input  [31:0] datain,
  input  CLK,
  output [31:0] dataout,
  output addr_illegal
);

  wire comparator_1_eq;
  wire [15:0] bit_extender_1_out;

  Bit_Extender #(.in_width(32)) bit_extender_1 (.in(addr), .out(bit_extender_1_out));
  RAM_64KByte ram_64kbyte_1 (
    .OpMemory(OpMemory), .WriteEnable(WriteEnable), .ReadEnable(ReadEnable), .CLK(CLK),
    .addr(bit_extender_1_out), .datain(datain), .OpByte(OpByte), .dataout(dataout));
  Comparator #(.mode("unsigned"), .width(14)) comparator_1 (
    .a(addr[31:18]), .b({14{1'b0}}), .eq(comparator_1_eq));  // open: gt, lt
  not not_1 (addr_illegal, comparator_1_eq);

  // Notes on the sheet:
  //   addr: initial=0xfffff
endmodule

module IF_ID (
  input  IsXor_in,
  input  Choice_in,
  input  [31:0] nPC_in,
  input  [4:0] rs_in,
  input  [4:0] rt_in,
  input  [4:0] rd_in,
  input  RegDst_in,
  input  [15:0] rawImm_in,
  input  ALUSrc_in,
  input  ImmPos_in,
  input  [3:0] InnerOp_in,
  input  Branch_in,
  input  MemRead_in,
  input  MemWrite_in,
  input  Jcond_in,
  input  OpMemory_in,
  input  OpByte_in,
  input  MemReg_in,
  input  RegWrite_in,
  input  STP_in,
  input  flush,
  input  WE,
  input  CLK,
  output isXor_out,
  output Choice_out,
  output [31:0] nPC_out,
  output [4:0] rs_out,
  output [4:0] rt_out,
  output [4:0] rd_out,
  output RegDst_out,
  output [15:0] rawImm_out,
  output ALUSrc_out,
  output ImmPos_out,
  output [3:0] InnerOp_out,
  output Branch_out,
  output MemRead_out,
  output MemWrite_out,
  output Jcond_out,
  output OpMemory_out,
  output OpByte_out,
  output MemReg_out,
  output RegWrite_out,
  output STP_out
);

  Register #(.width(1)) register_1 (.D(IsXor_in), .en(WE), .clk(CLK), .Q(isXor_out), .clr(flush));
  Register #(.width(1)) register_2 (.D(Choice_in), .en(WE), .clk(CLK), .Q(Choice_out), .clr(flush));
  Register #(.width(32)) register_3 (.D(nPC_in), .en(WE), .clk(CLK), .Q(nPC_out), .clr(flush));
  Register #(.width(5)) register_4 (.D(rs_in), .en(WE), .clk(CLK), .Q(rs_out), .clr(flush));
  Register #(.width(5)) register_5 (.D(rt_in), .en(WE), .clk(CLK), .Q(rt_out), .clr(flush));
  Register #(.width(5)) register_6 (.D(rd_in), .en(WE), .clk(CLK), .Q(rd_out), .clr(flush));
  Register #(.width(1)) register_7 (.D(RegDst_in), .en(WE), .clk(CLK), .Q(RegDst_out), .clr(flush));
  Register #(.width(16)) register_8 (.D(rawImm_in), .en(WE), .clk(CLK), .Q(rawImm_out), .clr(flush));
  Register #(.width(1)) register_9 (.D(ALUSrc_in), .en(WE), .clk(CLK), .Q(ALUSrc_out), .clr(flush));
  Register #(.width(1)) register_10 (.D(ImmPos_in), .en(WE), .clk(CLK), .Q(ImmPos_out), .clr(flush));
  Register #(.width(4)) register_11 (.D(InnerOp_in), .en(WE), .clk(CLK), .Q(InnerOp_out), .clr(flush));
  Register #(.width(1)) register_12 (.D(Branch_in), .en(WE), .clk(CLK), .Q(Branch_out), .clr(flush));
  Register #(.width(1)) register_13 (.D(MemRead_in), .en(WE), .clk(CLK), .Q(MemRead_out), .clr(flush));
  Register #(.width(1)) register_14 (.D(MemWrite_in), .en(WE), .clk(CLK), .Q(MemWrite_out), .clr(flush));
  Register #(.width(1)) register_15 (.D(Jcond_in), .en(WE), .clk(CLK), .Q(Jcond_out), .clr(flush));
  Register #(.width(1)) register_16 (.D(OpMemory_in), .en(WE), .clk(CLK), .Q(OpMemory_out), .clr(flush));
  Register #(.width(1)) register_17 (.D(OpByte_in), .en(WE), .clk(CLK), .Q(OpByte_out), .clr(flush));
  Register #(.width(1)) register_18 (.D(MemReg_in), .en(WE), .clk(CLK), .Q(MemReg_out), .clr(flush));
  Register #(.width(1)) register_19 (.D(RegWrite_in), .en(WE), .clk(CLK), .Q(RegWrite_out), .clr(flush));
  Register #(.width(1)) register_20 (.D(STP_in), .en(WE), .clk(CLK), .Q(STP_out), .clr(flush));
endmodule

module ID_EX (
  input  isXor_in,
  input  [31:0] rdata1_in,
  input  [31:0] rdata2_in,
  input  Choice_in,
  input  [31:0] nPC_in,
  input  [4:0] rs_in,
  input  [4:0] rt_in,
  input  [4:0] rd_in,
  input  RegDst_in,
  input  [15:0] rawImm_in,
  input  ALUSrc_in,
  input  ImmPos_in,
  input  [3:0] InnerOp_in,
  input  Branch_in,
  input  MemRead_in,
  input  MemWrite_in,
  input  Jcond_in,
  input  OpMemory_in,
  input  OpByte_in,
  input  MemReg_in,
  input  RegWrite_in,
  input  STP_in,
  input  WE,
  input  CLK,
  output isXor_out,
  output [31:0] rdata1_out,
  output [31:0] rdata2_out,
  output Choice_out,
  output [31:0] nPC_out,
  output [4:0] rs_out,
  output [4:0] rt_out,
  output [4:0] rd_out,
  output RegDst_out,
  output [15:0] rawImm_out,
  output ALUSrc_out,
  output ImmPos_out,
  output [3:0] InnerOp_out,
  output Branch_out,
  output MemRead_out,
  output MemWrite_out,
  output Jcond_out,
  output OpMemory_out,
  output OpByte_out,
  output MemReg_out,
  output RegWrite_out,
  output STP_out
);

  Register #(.width(1)) register_1 (.D(isXor_in), .en(WE), .clk(CLK), .Q(isXor_out));  // open: clr
  Register #(.width(32)) register_2 (.D(rdata1_in), .en(WE), .clk(CLK), .Q(rdata1_out));  // open: clr
  Register #(.width(32)) register_3 (.D(rdata2_in), .en(WE), .clk(CLK), .Q(rdata2_out));  // open: clr
  Register #(.width(1)) register_4 (.D(Choice_in), .en(WE), .clk(CLK), .Q(Choice_out));  // open: clr
  Register #(.width(32)) register_5 (.D(nPC_in), .en(WE), .clk(CLK), .Q(nPC_out));  // open: clr
  Register #(.width(5)) register_6 (.D(rs_in), .en(WE), .clk(CLK), .Q(rs_out));  // open: clr
  Register #(.width(5)) register_7 (.D(rt_in), .en(WE), .clk(CLK), .Q(rt_out));  // open: clr
  Register #(.width(5)) register_8 (.D(rd_in), .en(WE), .clk(CLK), .Q(rd_out));  // open: clr
  Register #(.width(1)) register_9 (.D(RegDst_in), .en(WE), .clk(CLK), .Q(RegDst_out));  // open: clr
  Register #(.width(16)) register_10 (.D(rawImm_in), .en(WE), .clk(CLK), .Q(rawImm_out));  // open: clr
  Register #(.width(1)) register_11 (.D(ALUSrc_in), .en(WE), .clk(CLK), .Q(ALUSrc_out));  // open: clr
  Register #(.width(1)) register_12 (.D(ImmPos_in), .en(WE), .clk(CLK), .Q(ImmPos_out));  // open: clr
  Register #(.width(4)) register_13 (.D(InnerOp_in), .en(WE), .clk(CLK), .Q(InnerOp_out));  // open: clr
  Register #(.width(1)) register_14 (.D(Branch_in), .en(WE), .clk(CLK), .Q(Branch_out));  // open: clr
  Register #(.width(1)) register_15 (.D(MemRead_in), .en(WE), .clk(CLK), .Q(MemRead_out));  // open: clr
  Register #(.width(1)) register_16 (.D(MemWrite_in), .en(WE), .clk(CLK), .Q(MemWrite_out));  // open: clr
  Register #(.width(1)) register_17 (.D(Jcond_in), .en(WE), .clk(CLK), .Q(Jcond_out));  // open: clr
  Register #(.width(1)) register_18 (.D(OpMemory_in), .en(WE), .clk(CLK), .Q(OpMemory_out));  // open: clr
  Register #(.width(1)) register_19 (.D(OpByte_in), .en(WE), .clk(CLK), .Q(OpByte_out));  // open: clr
  Register #(.width(1)) register_20 (.D(MemReg_in), .en(WE), .clk(CLK), .Q(MemReg_out));  // open: clr
  Register #(.width(1)) register_21 (.D(RegWrite_in), .en(WE), .clk(CLK), .Q(RegWrite_out));  // open: clr
  Register #(.width(1)) register_22 (.D(STP_in), .en(WE), .clk(CLK), .Q(STP_out));  // open: clr
endmodule

module EX_MEM (
  input  [31:0] res_in,
  input  MemRead_in,
  input  MemWrite_in,
  input  [4:0] Regwaddr_in,
  input  OpMemory_in,
  input  OpByte_in,
  input  MemReg_in,
  input  RegWrite_in,
  input  STP_in,
  input  [31:0] MemWriteData_in,
  input  WE,
  input  CLK,
  output [31:0] res_out,
  output MemRead_out,
  output MemWrite_out,
  output [4:0] Regwaddr_out,
  output OpMemory_out,
  output OpByte_out,
  output MemReg_out,
  output RegWrite_out,
  output STP_out,
  output [31:0] MemWriteData_out
);

  Register #(.width(32)) register_1 (.D(res_in), .en(WE), .clk(CLK), .Q(res_out));  // open: clr
  Register #(.width(1)) register_2 (.D(MemRead_in), .en(WE), .clk(CLK), .Q(MemRead_out));  // open: clr
  Register #(.width(1)) register_3 (.D(MemWrite_in), .en(WE), .clk(CLK), .Q(MemWrite_out));  // open: clr
  Register #(.width(5)) register_4 (.D(Regwaddr_in), .en(WE), .clk(CLK), .Q(Regwaddr_out));  // open: clr
  Register #(.width(1)) register_5 (.D(OpMemory_in), .en(WE), .clk(CLK), .Q(OpMemory_out));  // open: clr
  Register #(.width(1)) register_6 (.D(OpByte_in), .en(WE), .clk(CLK), .Q(OpByte_out));  // open: clr
  Register #(.width(1)) register_7 (.D(MemReg_in), .en(WE), .clk(CLK), .Q(MemReg_out));  // open: clr
  Register #(.width(1)) register_8 (.D(RegWrite_in), .en(WE), .clk(CLK), .Q(RegWrite_out));  // open: clr
  Register #(.width(1)) register_9 (.D(STP_in), .en(WE), .clk(CLK), .Q(STP_out));  // open: clr
  Register #(.width(32)) register_10 (.D(MemWriteData_in), .en(WE), .clk(CLK), .Q(MemWriteData_out));  // open: clr
endmodule

module MEM_WB (
  input  [31:0] WriteBackData_in,
  input  [4:0] Regwaddr_in,
  input  RegWrite_in,
  input  STP_in,
  input  WE,
  input  CLK,
  output [31:0] WriteBackDate_out,
  output [4:0] Regwaddr_out,
  output RegWrite_out,
  output STP_out
);

  Register #(.width(32)) register_1 (.D(WriteBackData_in), .en(WE), .clk(CLK), .Q(WriteBackDate_out));  // open: clr
  Register #(.width(5)) register_2 (.D(Regwaddr_in), .en(WE), .clk(CLK), .Q(Regwaddr_out));  // open: clr
  Register #(.width(1)) register_3 (.D(RegWrite_in), .en(WE), .clk(CLK), .Q(RegWrite_out));  // open: clr
  Register #(.width(1)) register_4 (.D(STP_in), .en(WE), .clk(CLK), .Q(STP_out));  // open: clr
endmodule

module BypassUnit_EX (
  input  [4:0] rs,
  input  [4:0] rt,
  input  RegWrite_EX,
  input  [4:0] waddr_EX,
  input  RegWrite_WB,
  input  [4:0] waddr_WB,
  output [1:0] ForwardA,
  output [1:0] ForwardB
);

  wire comparator_1_eq, comparator_2_eq, comparator_3_eq, comparator_4_eq, comparator_5_eq, comparator_6_eq,
       not_1_out, not_2_out, not_3_out, not_4_out;

  Comparator #(.mode("unsigned"), .width(5)) comparator_1 (
    .a(waddr_EX), .b({5{1'b0}}), .eq(comparator_1_eq));  // open: gt, lt
  Comparator #(.mode("unsigned"), .width(5)) comparator_2 (.a(waddr_EX), .b(rs), .eq(comparator_2_eq));  // open: gt, lt
  Comparator #(.mode("unsigned"), .width(5)) comparator_3 (.a(waddr_EX), .b(rt), .eq(comparator_3_eq));  // open: gt, lt
  Comparator #(.mode("unsigned"), .width(5)) comparator_4 (
    .a(waddr_WB), .b({5{1'b0}}), .eq(comparator_4_eq));  // open: gt, lt
  Comparator #(.mode("unsigned"), .width(5)) comparator_5 (.a(waddr_WB), .b(rs), .eq(comparator_5_eq));  // open: gt, lt
  Comparator #(.mode("unsigned"), .width(5)) comparator_6 (.a(waddr_WB), .b(rt), .eq(comparator_6_eq));  // open: gt, lt
  not not_1 (not_1_out, comparator_1_eq);
  not not_2 (not_2_out, comparator_4_eq);
  and and_1 (ForwardB[1], RegWrite_EX, not_1_out, comparator_3_eq);
  and and_2 (ForwardA[1], RegWrite_EX, not_1_out, comparator_2_eq);
  not not_3 (not_3_out, ForwardA[1]);
  not not_4 (not_4_out, ForwardB[1]);
  and and_3 (ForwardB[0], not_4_out, RegWrite_WB, not_2_out, comparator_6_eq);
  and and_4 (ForwardA[0], not_3_out, RegWrite_WB, not_2_out, comparator_5_eq);

  // Notes on the sheet:
  //   namely,ForwardRs
endmodule

module RiskControlUnit (
  input  MemRead_EX,
  input  [4:0] RegWrite_EX,
  input  [4:0] rs_ID,
  input  [4:0] rt_ID,
  output is_risk
);

  wire comparator_1_eq, comparator_2_eq, or_1_out;

  Comparator #(.mode("unsigned"), .width(5)) comparator_1 (
    .a(rs_ID), .b(RegWrite_EX), .eq(comparator_1_eq));  // open: gt, lt
  Comparator #(.mode("unsigned"), .width(5)) comparator_2 (
    .a(rt_ID), .b(RegWrite_EX), .eq(comparator_2_eq));  // open: gt, lt
  or or_1 (or_1_out, comparator_1_eq, comparator_2_eq);
  and and_1 (is_risk, MemRead_EX, or_1_out);
endmodule

module RAM_64KByte (
  input  OpMemory,
  input  WriteEnable,
  input  ReadEnable,
  input  CLK,
  input  [15:0] addr,
  input  [31:0] datain,
  input  OpByte,
  output [31:0] dataout
);

  wire and_1_out, and_2_out;
  wire [7:0] bit_extender_1_out, multiplexer_3_out;
  wire [31:0] bit_extender_2_out, multiplexer_1_out, multiplexer_2_out, ram_1_dout;

  Bit_Extender #(.in_width(32), .out_width(8)) bit_extender_1 (.in(datain), .out(bit_extender_1_out));
  and and_1 (and_1_out, OpMemory, WriteEnable);
  and and_2 (and_2_out, OpMemory, ReadEnable);
  Multiplexer #(.select(2), .width(32)) multiplexer_1 (
    .in0({ram_1_dout[31:8], bit_extender_1_out}),
    .in1({ram_1_dout[31:16], bit_extender_1_out, ram_1_dout[7:0]}),
    .in2({ram_1_dout[31:24], bit_extender_1_out, ram_1_dout[15:0]}),
    .in3({bit_extender_1_out, ram_1_dout[23:0]}), .out(multiplexer_1_out), .sel(addr[1:0]));
  Multiplexer #(.width(32)) multiplexer_2 (
    .in0(datain), .in1(multiplexer_1_out), .out(multiplexer_2_out), .sel(OpByte));
  RAM #(.addrWidth(14), .asyncread("true"), .dataWidth(32)) ram_1 (
    .addr(addr[15:2]), .we(and_1_out), .oe(and_2_out), .clk(CLK), .din(multiplexer_2_out), .dout(ram_1_dout));
  Multiplexer #(.select(2), .width(8)) multiplexer_3 (
    .in0(ram_1_dout[7:0]), .in1(ram_1_dout[15:8]), .in2(ram_1_dout[23:16]), .in3(ram_1_dout[31:24]),
    .out(multiplexer_3_out), .sel(addr[1:0]));
  assign bit_extender_2_out = {{24{1'b0}}, multiplexer_3_out};  // Bit_Extender bit_extender_2
  Multiplexer #(.width(32)) multiplexer_4 (.in0(ram_1_dout), .in1(bit_extender_2_out), .out(dataout), .sel(OpByte));
  // Probe on dataout

  // Notes on the sheet:
  //   addr: initial=0xfffff
endmodule

module BTB (
  input  [31:0] PC_IF,
  input  Branch_IF,
  input  [31:0] PC_EX,
  input  Branch_EX,
  input  Cond,
  input  CLK,
  output CondFit
);

  wire comparator_1_eq, comparator_1_gt, comparator_2_lt, comparator_3_gt, multiplexer_1_out, or_1_out,
       random_1_out;
  wire [31:0] adder_1_out, multiplexer_3_out, multiplexer_4_out, multiplexer_5_out,
       rawrigisterfile_128_1_rdata1, rawrigisterfile_128_1_rdata2, subtractor_1_out;

  RawRigisterFile_128 rawrigisterfile_128_1 (
    .raddr1(PC_IF[8:2]), .raddr2(PC_EX[8:2]), .waddr(PC_EX[8:2]), .wdata(multiplexer_5_out), .wen(Branch_EX),
    .CLK(CLK), .rdata1(rawrigisterfile_128_1_rdata1), .rdata2(rawrigisterfile_128_1_rdata2));
  Comparator #(.width(32)) comparator_1 (
    .a(rawrigisterfile_128_1_rdata1), .b({32{1'b0}}), .gt(comparator_1_gt), .eq(comparator_1_eq));  // open: lt
  // NOT_Gate not_1 has open pins: in=1'b1, out=open
  Subtractor #(.width(32)) subtractor_1 (
    .a(rawrigisterfile_128_1_rdata2), .b(32'h1), .out(subtractor_1_out));  // open: bin, bout
  Adder #(.width(32)) adder_1 (.a(rawrigisterfile_128_1_rdata2), .b(32'h1), .out(adder_1_out));  // open: cin, cout
  Multiplexer multiplexer_1 (.in0(comparator_1_eq), .in1(1'b0), .out(multiplexer_1_out), .sel(random_1_out));
  Multiplexer multiplexer_2 (.in0(1'b0), .in1(or_1_out), .out(CondFit), .sel(Branch_IF));
  or or_1 (or_1_out, comparator_1_gt, multiplexer_1_out);
  Comparator #(.width(32)) comparator_2 (.a(subtractor_1_out), .b(32'hfffffffe), .lt(comparator_2_lt));  // open: gt, eq
  Comparator #(.width(32)) comparator_3 (.a(adder_1_out), .b(32'h2), .gt(comparator_3_gt));  // open: eq, lt
  Random #(.seed(463), .width(1)) random_1 (.clk(CLK), .out(random_1_out));  // open: clr, next
  Multiplexer #(.width(32)) multiplexer_3 (
    .in0(subtractor_1_out), .in1(32'hfffffffe), .out(multiplexer_3_out), .sel(comparator_2_lt));
  Multiplexer #(.width(32)) multiplexer_4 (
    .in0(adder_1_out), .in1(32'h2), .out(multiplexer_4_out), .sel(comparator_3_gt));
  Multiplexer #(.width(32)) multiplexer_5 (
    .in0(multiplexer_3_out), .in1(multiplexer_4_out), .out(multiplexer_5_out), .sel(Cond));

  // Notes on the sheet:
  //   default:
endmodule

module Raw_RigisterFile_8 (
  input  wen,
  input  [31:0] wdata,
  input  [2:0] waddr,
  input  CLK,
  input  [2:0] raddr1,
  input  [2:0] raddr2,
  output [31:0] rdata1,
  output [31:0] rdata2
);

  wire demultiplexer_1_out0, demultiplexer_1_out1, demultiplexer_1_out2, demultiplexer_1_out3,
       demultiplexer_1_out4, demultiplexer_1_out5, demultiplexer_1_out6, demultiplexer_1_out7;
  wire [31:0] register_1_q, register_2_q, register_3_q, register_4_q, register_5_q, register_6_q,
       register_7_q, register_8_q;

  Register #(.width(32)) register_1 (.D(wdata), .en(demultiplexer_1_out0), .clk(CLK), .Q(register_1_q));  // open: clr
  Register #(.width(32)) register_2 (.D(wdata), .en(demultiplexer_1_out2), .clk(CLK), .Q(register_2_q));  // open: clr
  Register #(.width(32)) register_3 (.D(wdata), .en(demultiplexer_1_out4), .clk(CLK), .Q(register_3_q));  // open: clr
  Register #(.width(32)) register_4 (.D(wdata), .en(demultiplexer_1_out6), .clk(CLK), .Q(register_4_q));  // open: clr
  Demultiplexer #(.select(3)) demultiplexer_1 (
    .out0(demultiplexer_1_out0), .out1(demultiplexer_1_out1), .out2(demultiplexer_1_out2),
    .out3(demultiplexer_1_out3), .out4(demultiplexer_1_out4), .out5(demultiplexer_1_out5),
    .out6(demultiplexer_1_out6), .out7(demultiplexer_1_out7), .in(wen), .sel(waddr));
  Register #(.width(32)) register_5 (.D(wdata), .en(demultiplexer_1_out1), .clk(CLK), .Q(register_5_q));  // open: clr
  Register #(.width(32)) register_6 (.D(wdata), .en(demultiplexer_1_out3), .clk(CLK), .Q(register_6_q));  // open: clr
  Register #(.width(32)) register_7 (.D(wdata), .en(demultiplexer_1_out5), .clk(CLK), .Q(register_7_q));  // open: clr
  Register #(.width(32)) register_8 (.D(wdata), .en(demultiplexer_1_out7), .clk(CLK), .Q(register_8_q));  // open: clr
  Multiplexer #(.select(3), .width(32)) multiplexer_1 (
    .in0(register_1_q), .in1(register_5_q), .in2(register_2_q), .in3(register_6_q), .in4(register_3_q),
    .in5(register_7_q), .in6(register_4_q), .in7(register_8_q), .out(rdata1), .sel(raddr1));
  Multiplexer #(.select(3), .width(32)) multiplexer_2 (
    .in0(register_1_q), .in1(register_5_q), .in2(register_2_q), .in3(register_6_q), .in4(register_3_q),
    .in5(register_7_q), .in6(register_4_q), .in7(register_8_q), .out(rdata2), .sel(raddr2));
  // Probe on register_1_q
  // Probe on register_5_q
  // Probe on register_2_q
  // Probe on register_6_q
  // Probe on register_3_q
  // Probe on register_7_q
  // Probe on register_4_q
  // Probe on register_8_q

  // Notes on the sheet:
  //   wen: initial=0x1
endmodule

module Raw_RigisterFile_32 (
  input  wen,
  input  [31:0] wdata,
  input  [4:0] waddr,
  input  CLK,
  input  [4:0] raddr1,
  input  [4:0] raddr2,
  output [31:0] rdata1,
  output [31:0] rdata2
);

  wire demultiplexer_1_out0, demultiplexer_1_out1, demultiplexer_1_out2, demultiplexer_1_out3;
  wire [31:0] raw_rigisterfile_8_1_rdata1, raw_rigisterfile_8_1_rdata2, raw_rigisterfile_8_2_rdata1,
       raw_rigisterfile_8_2_rdata2, raw_rigisterfile_8_3_rdata1, raw_rigisterfile_8_3_rdata2,
       raw_rigisterfile_8_4_rdata1, raw_rigisterfile_8_4_rdata2;

  Demultiplexer #(.select(2)) demultiplexer_1 (
    .out0(demultiplexer_1_out0), .out1(demultiplexer_1_out1), .out2(demultiplexer_1_out2),
    .out3(demultiplexer_1_out3), .in(wen), .sel(waddr[4:3]));
  Raw_RigisterFile_8 raw_rigisterfile_8_1 (
    .wen(demultiplexer_1_out0), .wdata(wdata), .waddr(waddr[2:0]), .CLK(CLK), .raddr1(raddr1[2:0]),
    .raddr2(raddr2[2:0]), .rdata1(raw_rigisterfile_8_1_rdata1), .rdata2(raw_rigisterfile_8_1_rdata2));
  Raw_RigisterFile_8 raw_rigisterfile_8_2 (
    .wen(demultiplexer_1_out1), .wdata(wdata), .waddr(waddr[2:0]), .CLK(CLK), .raddr1(raddr1[2:0]),
    .raddr2(raddr2[2:0]), .rdata1(raw_rigisterfile_8_2_rdata1), .rdata2(raw_rigisterfile_8_2_rdata2));
  Raw_RigisterFile_8 raw_rigisterfile_8_3 (
    .wen(demultiplexer_1_out2), .wdata(wdata), .waddr(waddr[2:0]), .CLK(CLK), .raddr1(raddr1[2:0]),
    .raddr2(raddr2[2:0]), .rdata1(raw_rigisterfile_8_3_rdata1), .rdata2(raw_rigisterfile_8_3_rdata2));
  Raw_RigisterFile_8 raw_rigisterfile_8_4 (
    .wen(demultiplexer_1_out3), .wdata(wdata), .waddr(waddr[2:0]), .CLK(CLK), .raddr1(raddr1[2:0]),
    .raddr2(raddr2[2:0]), .rdata1(raw_rigisterfile_8_4_rdata1), .rdata2(raw_rigisterfile_8_4_rdata2));
  Multiplexer #(.select(2), .width(32)) multiplexer_1 (
    .in0(raw_rigisterfile_8_1_rdata1), .in1(raw_rigisterfile_8_2_rdata1), .in2(raw_rigisterfile_8_3_rdata1),
    .in3(raw_rigisterfile_8_4_rdata1), .out(rdata1), .sel(raddr1[4:3]));
  Multiplexer #(.select(2), .width(32)) multiplexer_2 (
    .in0(raw_rigisterfile_8_1_rdata2), .in1(raw_rigisterfile_8_2_rdata2), .in2(raw_rigisterfile_8_3_rdata2),
    .in3(raw_rigisterfile_8_4_rdata2), .out(rdata2), .sel(raddr2[4:3]));

  // Notes on the sheet:
  //   wen: initial=0x1
endmodule

module RawRigisterFile_128 (
  input  [6:0] raddr1,
  input  [6:0] raddr2,
  input  [6:0] waddr,
  input  [31:0] wdata,
  input  wen,
  input  CLK,
  output [31:0] rdata1,
  output [31:0] rdata2
);

  wire demultiplexer_1_out0, demultiplexer_1_out1, demultiplexer_1_out2, demultiplexer_1_out3;
  wire [31:0] raw_rigisterfile_32_1_rdata1, raw_rigisterfile_32_1_rdata2, raw_rigisterfile_32_2_rdata1,
       raw_rigisterfile_32_2_rdata2, raw_rigisterfile_32_3_rdata1, raw_rigisterfile_32_3_rdata2,
       raw_rigisterfile_32_4_rdata1, raw_rigisterfile_32_4_rdata2;

  Demultiplexer #(.select(2)) demultiplexer_1 (
    .out0(demultiplexer_1_out0), .out1(demultiplexer_1_out1), .out2(demultiplexer_1_out2),
    .out3(demultiplexer_1_out3), .in(wen), .sel(waddr[1:0]));
  Raw_RigisterFile_32 raw_rigisterfile_32_1 (
    .wen(demultiplexer_1_out0), .wdata(wdata), .waddr(waddr[6:2]), .CLK(CLK), .raddr1(raddr1[6:2]),
    .raddr2(raddr2[6:2]), .rdata1(raw_rigisterfile_32_1_rdata1), .rdata2(raw_rigisterfile_32_1_rdata2));
  Raw_RigisterFile_32 raw_rigisterfile_32_2 (
    .wen(demultiplexer_1_out1), .wdata(wdata), .waddr(waddr[6:2]), .CLK(CLK), .raddr1(raddr1[6:2]),
    .raddr2(raddr2[6:2]), .rdata1(raw_rigisterfile_32_2_rdata1), .rdata2(raw_rigisterfile_32_2_rdata2));
  Raw_RigisterFile_32 raw_rigisterfile_32_3 (
    .wen(demultiplexer_1_out2), .wdata(wdata), .waddr(waddr[6:2]), .CLK(CLK), .raddr1(raddr1[6:2]),
    .raddr2(raddr2[6:2]), .rdata1(raw_rigisterfile_32_3_rdata1), .rdata2(raw_rigisterfile_32_3_rdata2));
  Raw_RigisterFile_32 raw_rigisterfile_32_4 (
    .wen(demultiplexer_1_out3), .wdata(wdata), .waddr(waddr[6:2]), .CLK(CLK), .raddr1(raddr1[6:2]),
    .raddr2(raddr2[6:2]), .rdata1(raw_rigisterfile_32_4_rdata1), .rdata2(raw_rigisterfile_32_4_rdata2));
  Multiplexer #(.select(2), .width(32)) multiplexer_1 (
    .in0(raw_rigisterfile_32_1_rdata1), .in1(raw_rigisterfile_32_2_rdata1),
    .in2(raw_rigisterfile_32_3_rdata1), .in3(raw_rigisterfile_32_4_rdata1), .out(rdata1), .sel(raddr1[1:0]));
  Multiplexer #(.select(2), .width(32)) multiplexer_2 (
    .in0(raw_rigisterfile_32_1_rdata2), .in1(raw_rigisterfile_32_2_rdata2),
    .in2(raw_rigisterfile_32_3_rdata2), .in3(raw_rigisterfile_32_4_rdata2), .out(rdata2), .sel(raddr2[1:0]));

  // Notes on the sheet:
  //   wen: initial=0x1
endmodule

module UBcheck (
  input  [5:0] opcode,
  input  [5:0] func,
  output NONEUB
);

  wire and_1_out, comparator_1_eq, comparator_2_eq, comparator_3_eq, not_1_out, not_2_out;

  Comparator #(.width(6)) comparator_1 (.a(opcode), .b({6{1'b0}}), .eq(comparator_1_eq));  // open: gt, lt
  Comparator #(.width(6)) comparator_2 (
    .a(opcode), .b({6{1'b0}}), .eq(comparator_2_eq), .lt(comparator_2_eq));  // open: gt
  Comparator #(.width(6)) comparator_3 (.a(func), .b({6{1'b0}}), .eq(comparator_3_eq));  // open: gt, lt
  and and_1 (and_1_out, comparator_2_eq, comparator_3_eq);
  not not_1 (not_1_out, comparator_1_eq);
  not not_2 (not_2_out, and_1_out);

  assign NONEUB = 1'b1;

  // Notes on the sheet:
  //   only opcode
  //   opcode and func
endmodule

module NEW_IF_UNIT (
  input  [5:0] ins,
  input  [5:0] func,
  output RegDst,
  output RegWrite,
  output ALUSrc,
  output Branch,
  output MemRead,
  output MemWrite,
  output MemReg,
  output ImmPos,
  output [2:0] ALUOp,
  output Jcond,
  output STP,
  output isXor
);

  wire and_1_out, and_2_out, and_4_out, comparator_2_eq, comparator_3_eq, comparator_4_eq, comparator_5_eq,
       comparator_6_eq, comparator_8_eq, comparator_9_eq, comparator_12_eq, comparator_13_eq,
       comparator_14_eq, comparator_15_eq;

  Comparator #(.mode("unsigned"), .width(6)) comparator_1 (.a(ins), .b(6'b100011), .eq(MemRead));  // open: gt, lt
  Comparator #(.mode("unsigned"), .width(6)) comparator_2 (
    .a(ins), .b({6{1'b0}}), .eq(comparator_2_eq));  // open: gt, lt
  Comparator #(.mode("unsigned"), .width(6)) comparator_3 (
    .a(func), .b(6'b100001), .eq(comparator_3_eq));  // open: gt, lt
  Comparator #(.mode("unsigned"), .width(6)) comparator_4 (
    .a(ins), .b({6{1'b0}}), .eq(comparator_4_eq));  // open: gt, lt
  Comparator #(.mode("unsigned"), .width(6)) comparator_5 (
    .a(func), .b(6'b100010), .eq(comparator_5_eq));  // open: gt, lt
  Comparator #(.mode("unsigned"), .width(6)) comparator_6 (
    .a(ins), .b(6'b001101), .eq(comparator_6_eq));  // open: gt, lt
  Comparator #(.mode("unsigned"), .width(6)) comparator_7 (.a(ins), .b(6'b001111), .eq(ImmPos));  // open: gt, lt
  Comparator #(.mode("unsigned"), .width(6)) comparator_8 (
    .a(ins), .b(6'b000101), .eq(comparator_8_eq));  // open: gt, lt
  Comparator #(.mode("unsigned"), .width(6)) comparator_9 (.b(6'b000100), .eq(comparator_9_eq));  // open: a, gt, lt
  Comparator #(.mode("unsigned"), .width(6)) comparator_10 (.a(ins), .b(6'b101011), .eq(MemWrite));  // open: gt, lt
  Comparator #(.mode("unsigned"), .width(6)) comparator_11 (.a(ins), .b({6{1'b1}}), .eq(STP));  // open: gt, lt
  Comparator #(.mode("unsigned"), .width(6)) comparator_12 (
    .a(ins), .b({6{1'b0}}), .eq(comparator_12_eq));  // open: gt, lt
  Comparator #(.mode("unsigned"), .width(6)) comparator_13 (
    .a(func), .b(6'b100011), .eq(comparator_13_eq));  // open: gt, lt
  Comparator #(.mode("unsigned"), .width(6)) comparator_14 (
    .a(ins), .b({6{1'b0}}), .eq(comparator_14_eq));  // open: gt, lt
  Comparator #(.mode("unsigned"), .width(6)) comparator_15 (
    .a(func), .b(6'b100111), .eq(comparator_15_eq));  // open: gt, lt
  and and_1 (and_1_out, comparator_2_eq, comparator_3_eq);
  and and_2 (and_2_out, comparator_4_eq, comparator_5_eq);
  // AND_Gate and_3 has open pins: in0=comparator_12_eq, in1=comparator_13_eq, out=open
  and and_4 (and_4_out, comparator_14_eq, comparator_15_eq);
  or or_1 (ALUOp[1], and_1_out, and_2_out, 1'b0, and_4_out);
  or or_2 (ALUOp[2], ALUOp[1], comparator_6_eq);
  or or_3 (ALUOp[0], comparator_6_eq, ALUOp[1], comparator_8_eq, 1'b0);
  or or_4 (RegWrite, MemRead, ALUOp[1], comparator_6_eq, ImmPos);
  or or_5 (ALUSrc, comparator_6_eq, ImmPos, MemRead, MemWrite);
  or or_6 (Branch, comparator_8_eq, 1'b0);
  or or_7 (MemReg, ImmPos, ALUOp[1], comparator_6_eq, comparator_8_eq, 1'b0, MemWrite);

  assign isXor = 1'b0;
  assign Jcond = 1'b0;
  assign RegDst = ALUOp[1];

  // Notes on the sheet:
  //   addu
  //   sub
  //   ori
  //   lui
  //   bne
  //   beq！！！
  //   lw
  //   sw
  //   stp
  //   QM1
endmodule

module STPUnit (
  input  CLK,
  input  Reset,
  input  STP,
  output Status
);

  wire register_1_q;

  Register #(.width(1)) register_1 (.D(STP), .en(STP), .clk(CLK), .Q(register_1_q), .clr(Reset));
  or or_1 (Status, register_1_q, STP);
endmodule
